# Fritzing sketch Interruptor Conectado Modulo 02 v1.0 (saved by Fritzing 0.9.3b)
circuit board: 7cm x 5cm
breadboards: 1

parts:
  U1 = ESP8266 WiFi Module [part_number=ESP8266]
  R6 = Resistor [tolerance=±5% resistance=10k package=THT]
  D5 = Rectifier Diode [part_number=1N4001 package="300 mil [THT]"]
  R7 = Resistor [tolerance=±5% resistance=10k package=THT]
  D6 = Rectifier Diode [part_number=1N4001 package="300 mil [THT]"]
  Q7 = NPN-Transistor [package="TO92 [THT]"]
  Q6 = NPN-Transistor [package="TO92 [THT]"]
  R2 = Resistor [tolerance=±5% resistance=3.3k package=THT]
  R3 = Resistor [tolerance=±5% resistance=3.3k package=THT]
  R1 = Resistor [tolerance=±5% resistance=3.3k package=THT]
  K3 = OMRON PCB Power Relay – G5LE [part_number="G5LE-1\n" package=THT]
  Relay2 = screw terminal, 3 pins
  K4 = OMRON PCB Power Relay – G5LE [part_number="G5LE-1\n" package=THT]
  Relay3 = screw terminal, 3 pins
  C3 = Electrolytic Capacitor [capacitance=100µF voltage=16V package="100 mil [THT, electrolytic]"]
  C4 = Electrolytic Capacitor [capacitance=100µF voltage=16V package="100 mil [THT, electrolytic]"]
  C5 = Electrolytic Capacitor [capacitance=10µF voltage=16V package="100 mil [THT, electrolytic]"]
  DC_IN = screw terminal, 2 pins
  S3 = SWITCH-MOMENTARY-2 [package=tactile-pth-12mm]
  REG_3_3v = Voltage Regulator AMS1117 [package=sot223]
  REG_5V = Voltage Regulator [package=sot223]
  S4 = SWITCH-MOMENTARY-2 [package=tactile-pth-12mm]
  R8 = Resistor [tolerance=±5% resistance=3.3k package=THT]

nets:
  N1: U1.RXD, S4.1
  N2: U1.VCC, R2.Pin_1, R3.Pin_1, R1.Pin_1, C3.+, REG_3_3v.OUT, R8.Pin_1
  N3: U1.GPIO_0, R6.Pin_0, R2.Pin_0
  N4: U1.RST, R8.Pin_0
  N5: U1.GPIO_2, R7.Pin_0, R1.Pin_0
  N6: U1.CH_PD, R3.Pin_0
  GND: U1.GND, Q7.E, Q6.E, C3.-, C4.-, C5.-, DC_IN.pin1, S3.2, REG_3_3v.GND, REG_5V.ADJ, S4.2
  N7: U1.TXD, S3.1
  N8: R6.Pin_1, Q6.B
  5V: D5.cathode, D6.cathode, K3.COIL2, K4.COIL2, C4.+, REG_3_3v.IN, REG_5V.OUT
  N9: D5.anode, Q6.C, K3.COIL1
  N10: R7.Pin_1, Q7.B
  N11: D6.anode, Q7.C, K4.COIL1
  N12: K3.A, Relay2.pin1
  N13: K3.C, Relay2.pin2
  N14: K3.B, Relay2.pin3
  N15: K4.A, Relay3.pin1
  N16: K4.C, Relay3.pin2
  N17: K4.B, Relay3.pin3
  12V: C5.+, DC_IN.pin2, REG_5V.IN

custom parts:
  ESP8266 WiFi Module: Generic WiFi Module based on the ESP8266 with onboard PCB antenna and UART communications
